// Logisim project comp.circ as structural Verilog: 3 circuits, main circuit main
module main (
  output [7:0] out_1,
  output [7:0] out_2,
  output [3:0] out_3
);

  wire A_In, A_Out, Alu_Mode_1, Alu_Mode_2, Alu_Out, B_In, B_Out, bintodec_1_out_2, bintodec_1_out_3,
       bintodec_1_out_4, bintodec_1_out_5, bintodec_1_out_6, bintodec_1_out_7, bintodec_1_out_8,
       bintodec_1_out_9, bintodec_1_out_10, bintodec_1_out_11, bintodec_1_out_12, bintodec_1_out_13,
       bintodec_1_out_14, bintodec_1_out_15, bintodec_1_out_16, bintodec_1_out_17, bintodec_1_out_18,
       bintodec_1_out_19, bintodec_1_out_20, bintodec_1_out_21, bintodec_1_out_22, bintodec_1_out_23,
       bintodec_1_out_24, bintodec_1_out_25, clock_1_out, clock_2_out, clock_3_out, clock_4_out, clock_5_out,
       clock_6_out, clock_7_out, clock_9_out, Count_En, Count_Jump, Count_Out, decoder_1_out5, HLT,
       Instruction_In, Instruction_Out, not_1_out, or_1_out, Output_In, Ram_Adr_In, Ram_Data_In,
       Ram_Data_Out, RST;
  wire [2:0] counter_2_q;
  wire [3:0] Instructions, register_2_q, register_4_q;
  wire [7:0] A, adder_1_out, and_1_out, B, multiplexer_1_out, or_2_out, ram_1_dout, subtractor_1_out;

  Clock clock_1 (.out(clock_1_out));
  Clock clock_2 (.out(clock_2_out));
  not not_1 (not_1_out, clock_2_out);
  Register register_1 (.D(out_2), .en(A_In), .clk(clock_1_out), .Q(A), .clr(RST));
  Clock clock_3 (.out(clock_3_out));
  assign out_2 = A_Out ? A : 8'bz;  // Controlled_Buffer controlled_buffer_1
  Counter #(.max('hf), .width(4)) counter_1 (
    .load(Count_Jump), .D(out_2[3:0]), .count(Count_En), .Q(out_3), .clk(clock_4_out), .clr(RST));  // open: carry, up
  Clock clock_4 (.out(clock_4_out));
  Register #(.width(4)) register_2 (.D(out_2[3:0]), .en(Ram_Adr_In), .clk(clock_3_out), .Q(register_2_q), .clr(RST));
  Counter #(.max('h7), .width(3)) counter_2 (
    .Q(counter_2_q), .clk(not_1_out), .clr(or_1_out));  // open: load, D, count, carry, up
  or or_1 (or_1_out, RST, decoder_1_out5);
  Decoder #(.select(3)) decoder_1 (
    .out5(decoder_1_out5), .sel(counter_2_q));  // open: out0, out1, out2, out3, out4, out6, out7, en
  ROM #(.addrWidth(7), .dataWidth(16)) rom_1 (
    .addr({Instructions, counter_2_q}),
    .data({A_In, A_Out, B_In, Alu_Mode_1, Alu_Mode_2, Alu_Out, Count_En, Count_Out, Count_Jump, Instruction_In, Instruction_Out, Ram_Adr_In, Ram_Data_In, Ram_Data_Out, Output_In, HLT}));
  assign out_2 = Count_Out ? {4'b0000, out_3} : 8'bz;  // Controlled_Buffer controlled_buffer_2
  Clock clock_5 (.out(clock_5_out));
  Register register_3 (.D(out_2), .en(B_In), .clk(clock_6_out), .Q(B), .clr(RST));
  Clock clock_6 (.out(clock_6_out));
  RAM #(.addrWidth(4), .asyncread("true")) ram_1 (
    .addr(register_2_q), .we(Ram_Data_In), .clk(clock_5_out), .din(out_2), .dout(ram_1_dout));  // open: oe
  assign out_2 = B_Out ? B : 8'bz;  // Controlled_Buffer controlled_buffer_3
  Adder adder_1 (.a(A), .b(B), .out(adder_1_out));  // open: cin, cout
  Subtractor subtractor_1 (.a(A), .b(B), .out(subtractor_1_out));  // open: bin, bout
  assign and_1_out = A & B;  // AND_Gate and_1, 8 bits wide
  assign or_2_out = A | B;  // OR_Gate or_2, 8 bits wide
  assign out_2 = Ram_Data_Out ? ram_1_dout : 8'bz;  // Controlled_Buffer controlled_buffer_4
  assign out_2 = Alu_Out ? multiplexer_1_out : 8'bz;  // Controlled_Buffer controlled_buffer_5
  Multiplexer #(.select(2), .width(8)) multiplexer_1 (
    .in0(adder_1_out), .in1(subtractor_1_out), .in2(and_1_out), .in3(or_2_out), .out(multiplexer_1_out),
    .sel({Alu_Mode_2, Alu_Mode_1}));
  Register register_4 (.D(out_2), .en(Instruction_In), .clk(clock_7_out), .Q({Instructions, register_4_q}), .clr(RST));
  Clock clock_7 (.out(clock_7_out));
  assign out_2 = Instruction_Out ? {4'b0000, register_4_q} : 8'bz;  // Controlled_Buffer controlled_buffer_6
  Button button_1 (.out(RST));
  Clock clock_8 ();  // open: out
  Register register_5 (.D(out_2), .en(Output_In), .clk(clock_9_out), .Q(out_1), .clr(RST));
  Clock clock_9 (.out(clock_9_out));
  LED led_1 (.in(HLT));
  _7_Segment_Display u_7_segment_display_1 (
    .g(bintodec_1_out_2), .f(bintodec_1_out_3), .a(bintodec_1_out_4), .b(bintodec_1_out_5),
    .e(bintodec_1_out_6), .d(bintodec_1_out_7), .c(bintodec_1_out_8), .dp(bintodec_1_out_9));
  _7_Segment_Display u_7_segment_display_2 (
    .g(bintodec_1_out_10), .f(bintodec_1_out_11), .a(bintodec_1_out_12), .b(bintodec_1_out_13),
    .e(bintodec_1_out_14), .d(bintodec_1_out_15), .c(bintodec_1_out_16), .dp(bintodec_1_out_17));
  BinToDec bintodec_1 (
    .in_1(out_1), .out_2(bintodec_1_out_2), .out_10(bintodec_1_out_10), .out_18(bintodec_1_out_18),
    .out_3(bintodec_1_out_3), .out_11(bintodec_1_out_11), .out_19(bintodec_1_out_19),
    .out_4(bintodec_1_out_4), .out_12(bintodec_1_out_12), .out_20(bintodec_1_out_20),
    .out_5(bintodec_1_out_5), .out_13(bintodec_1_out_13), .out_21(bintodec_1_out_21),
    .out_6(bintodec_1_out_6), .out_14(bintodec_1_out_14), .out_22(bintodec_1_out_22),
    .out_7(bintodec_1_out_7), .out_15(bintodec_1_out_15), .out_23(bintodec_1_out_23),
    .out_8(bintodec_1_out_8), .out_16(bintodec_1_out_16), .out_24(bintodec_1_out_24),
    .out_9(bintodec_1_out_9), .out_17(bintodec_1_out_17), .out_25(bintodec_1_out_25));
  _7_Segment_Display u_7_segment_display_3 (
    .g(bintodec_1_out_18), .f(bintodec_1_out_19), .a(bintodec_1_out_20), .b(bintodec_1_out_21),
    .e(bintodec_1_out_22), .d(bintodec_1_out_23), .c(bintodec_1_out_24), .dp(bintodec_1_out_25));

  // Other names for the same wires on the sheet: B_U_S[7:0] = out_2; Count[3:0] = out_3; ANS[7:0] = out_1

  // Notes on the sheet:
  //   A Register
  //   Counter
  //   contents of rom_1 (hex, n*v repeats v):
  //   110 244 6*0 110 244 30 8004 4*0 110 244 30 2004 8400 0 0 0 110 244 30 2004 9400 0 0 0 110 244 30
  //   2004 8c00 0 0 0 110 244 30 2004 9c00 0 0 0 110 244 30 4008 4*0 110 244 8020 5*0 110 244 a0 5*0 110
  //   244 6*0 110 244 6*0 110 244 6*0 110 244 6*0 110 244 6*0 110 244 4002 5*0 110 244 1
  //   RAM
  //   B Register
  //   Control Logic
  //   ALU
  //   Instruction Register
  //   Output Register
endmodule

module G (
  input  [3:0] in_1,
  input  [2:0] in_2,
  input  in_3,
  input  [7:0] in_4,
  input  [7:0] in_5,
  input  [3:0] in_6,
  input  [3:0] in_7,
  input  [3:0] in_8,
  output [7:0] out_9
);

  wire button_1_out, clock_1_out, I_1, I_2, I_3, I_4, I_5, I_6, I_7, I_8, I_9, I_10, I_11, I_12, I_13, I_14,
       I_15, I_16;

  Button button_1 (.out(button_1_out));
  RAM #(.addrWidth(4), .asyncread("true")) ram_1 (
    .addr(in_6), .we(1'b1), .oe(1'b1), .clk(button_1_out), .din({in_7, in_8}), .dout(out_9));
  RAM #(.addrWidth(7), .asyncread("true"), .dataWidth(16)) ram_2 (
    .addr({in_1, in_2}), .we(in_3), .clk(clock_1_out), .din({in_4, in_5}),
    .dout({I_1, I_2, I_3, I_4, I_5, I_6, I_7, I_8, I_9, I_10, I_11, I_12, I_13, I_14, I_15, I_16}));  // open: oe
  Clock clock_1 (.out(clock_1_out));
endmodule

module BinToDec (
  input  [7:0] in_1,
  output out_2,
  output out_3,
  output out_4,
  output out_5,
  output out_6,
  output out_7,
  output out_8,
  output out_9,
  output out_10,
  output out_11,
  output out_12,
  output out_13,
  output out_14,
  output out_15,
  output out_16,
  output out_17,
  output out_18,
  output out_19,
  output out_20,
  output out_21,
  output out_22,
  output out_23,
  output out_24,
  output out_25
);

  wire [3:0] X, Y, Z;
  wire [7:0] multiplier_1_out, multiplier_2_out, subtractor_1_out;
  wire [7:4] divider_1_out, divider_2_out, subtractor_2_out;

  Divider divider_1 (.a(in_1), .b(8'h64), .out({divider_1_out, X}));  // open: upper, rem
  ROM #(.addrWidth(4)) rom_1 (.addr(X), .data({out_9, out_8, out_7, out_6, out_5, out_4, out_3, out_2}));
  ROM #(.addrWidth(4)) rom_2 (.addr(Y), .data({out_17, out_16, out_15, out_14, out_13, out_12, out_11, out_10}));
  ROM #(.addrWidth(4)) rom_3 (.addr(Z), .data({out_25, out_24, out_23, out_22, out_21, out_20, out_19, out_18}));
  Multiplier multiplier_1 (.a({divider_1_out, X}), .b(8'h64), .out(multiplier_1_out));  // open: cin, cout
  Subtractor subtractor_1 (.a(in_1), .b(multiplier_1_out), .out(subtractor_1_out));  // open: bin, bout
  Divider divider_2 (.a(subtractor_1_out), .b(8'ha), .out({divider_2_out, Y}));  // open: upper, rem
  Multiplier multiplier_2 (.a({divider_2_out, Y}), .b(8'ha), .out(multiplier_2_out));  // open: cin, cout
  Subtractor subtractor_2 (.a(subtractor_1_out), .b(multiplier_2_out), .out({subtractor_2_out, Z}));  // open: bin, bout

  // Notes on the sheet:
  //   contents of rom_1 (hex, n*v repeats v):
  //   7e 48 3d 6d 4b 67 77 4c 7f 6f
  //   contents of rom_2 (hex, n*v repeats v):
  //   7e 48 3d 6d 4b 67 77 4c 7f 6f
  //   contents of rom_3 (hex, n*v repeats v):
  //   7e 48 3d 6d 4b 67 77 4c 7f 6f
endmodule
